// Logisim project CPU.circ as structural Verilog: 8 circuits, main circuit ExampleConfigurationROM
module ExampleConfigurationROM (
  input  Breakpoint_A,
  input  Breakpoint_B,
  input  Breakpoint_C,
  input  Breakpoint_D,
  input  Breakpoint_E,
  input  [7:0] in_6,
  input  RESET,
  output WRITE_ACTIVE,
  output IO_ACTIVE,
  output IO_ENABLE
);

  wire and_1_out, and_2_out, and_3_out, and_4_out, and_5_out, and_6_out, and_7_out, and_8_out, and_9_out,
       and_10_out, and_11_out, and_12_out, and_13_out, and_14_out, and_15_out, and_16_out, CLOCK_out,
       comparator_1_eq, comparator_2_eq, comparator_3_eq, comparator_4_eq, comparator_5_eq, comparator_6_eq,
       comparator_7_eq, comparator_8_eq, comparator_9_eq, keyboard_1_avail, or_2_out, or_3_out, or_4_out;
  wire [7:0] au_1_fpu, controlled_buffer_1_out, keyboard_1_data, mcu_1_addr, mcu_1_out, mcu_1_seg,
       register_1_q, register_2_q, rom_1_data;

  MCU mcu_1 (
    .IO_ENABLE(IO_ENABLE), .IN(controlled_buffer_1_out), .ADDR(mcu_1_addr), .OUT(mcu_1_out), .CLK(and_3_out),
    .RST(RESET), .IO_ACTIVE(IO_ACTIVE), .WRITE_ACTIVE(WRITE_ACTIVE), .SEG(mcu_1_seg));
  or or_1 (IO_ENABLE, and_1_out, or_2_out);
  or or_2 (or_2_out, or_3_out, and_4_out);
  or or_3 (or_3_out, and_6_out, and_5_out);
  Clock CLOCK (.out(CLOCK_out));
  Comparator #(.mode("unsigned")) comparator_1 (.a(mcu_1_addr), .b({8{1'b1}}), .eq(comparator_1_eq));  // open: gt, lt
  Comparator #(.mode("unsigned")) comparator_2 (.a(mcu_1_addr), .b(8'hfe), .eq(comparator_2_eq));  // open: gt, lt
  Comparator #(.mode("unsigned")) comparator_3 (.a(mcu_1_addr), .b(8'hfd), .eq(comparator_3_eq));  // open: gt, lt
  Comparator #(.mode("unsigned")) comparator_4 (.a(mcu_1_addr), .b(8'hfc), .eq(comparator_4_eq));  // open: gt, lt
  // Probe on controlled_buffer_1_out
  // Probe on mcu_1_addr
  // Probe on mcu_1_seg
  // Probe on mcu_1_out
  and and_1 (and_1_out, ~or_2_out, ~IO_ACTIVE);  // AND_Gate
  Register register_1 (.D(mcu_1_out), .en(and_2_out), .Q(register_1_q), .clk(and_3_out), .clr(RESET));
  and and_2 (and_2_out, comparator_1_eq, IO_ACTIVE, WRITE_ACTIVE);
  and and_3 (and_3_out, CLOCK_out, ~or_4_out);  // AND_Gate
  and and_4 (and_4_out, comparator_2_eq, IO_ACTIVE);
  and and_5 (and_5_out, comparator_3_eq, IO_ACTIVE);
  and and_6 (and_6_out, comparator_4_eq, IO_ACTIVE);
  // Probe on {register_1_q, mcu_1_addr}
  AU au_1 (.INPUT(mcu_1_out), .CLK(and_3_out), .WRITE_EN(and_7_out), .RST(RESET), .READ_EN(and_4_out), .FPU(au_1_fpu));
  and and_7 (and_7_out, and_4_out, WRITE_ACTIVE);
  assign controlled_buffer_1_out = and_4_out ? au_1_fpu : 8'bz;  // Controlled_Buffer controlled_buffer_1
  Register register_2 (.D(mcu_1_out), .en(and_8_out), .Q(register_2_q), .clk(and_3_out), .clr(RESET));
  Hex_Digit_Display hex_digit_display_1 (.value(register_2_q[7:4]));  // open: dp
  and and_8 (and_8_out, and_5_out, WRITE_ACTIVE);
  and and_9 (and_9_out, ~mcu_1_out[7], WRITE_ACTIVE);  // AND_Gate
  and and_10 (and_10_out, mcu_1_out[7], WRITE_ACTIVE);
  and and_11 (and_11_out, and_6_out, and_3_out);
  Hex_Digit_Display hex_digit_display_2 (.value(register_2_q[3:0]));  // open: dp
  TTY #(.cols(80)) tty_1 (.data(mcu_1_out[6:0]), .clk(and_11_out), .we(and_9_out), .clr(RESET));
  Keyboard #(.buflen(80), .trigger("falling")) keyboard_1 (
    .clk(and_11_out), .re(and_10_out), .clr(RESET), .avail(keyboard_1_avail), .data(keyboard_1_data[6:0]));
  ROM #(.addrWidth(16)) rom_1 (.addr({register_1_q, mcu_1_addr}), .data(rom_1_data));  // open: sel
  assign controlled_buffer_1_out = and_1_out ? rom_1_data : 8'bz;  // Controlled_Buffer controlled_buffer_2
  or or_4 (or_4_out, and_12_out, and_13_out, and_14_out, and_15_out, and_16_out);
  assign controlled_buffer_1_out = and_5_out ? in_6 : 8'bz;  // Controlled_Buffer controlled_buffer_3
  not not_1 (keyboard_1_data[7], keyboard_1_avail);
  assign controlled_buffer_1_out = and_6_out ? keyboard_1_data : 8'bz;  // Controlled_Buffer controlled_buffer_4
  Comparator #(.width(16), .mode("unsigned")) comparator_5 (
    .a({register_1_q, mcu_1_addr}), .b(16'h20), .eq(comparator_5_eq));  // open: gt, lt
  and and_12 (and_12_out, comparator_5_eq, Breakpoint_A);
  Comparator #(.width(16), .mode("unsigned")) comparator_6 (
    .a({register_1_q, mcu_1_addr}), .b(16'ha8), .eq(comparator_6_eq));  // open: gt, lt
  and and_13 (and_13_out, comparator_6_eq, Breakpoint_B);
  Comparator #(.width(16), .mode("unsigned")) comparator_7 (
    .a({register_1_q, mcu_1_addr}), .b(16'h47), .eq(comparator_7_eq));  // open: gt, lt
  and and_14 (and_14_out, comparator_7_eq, Breakpoint_C);
  Comparator #(.width(16), .mode("unsigned")) comparator_8 (
    .a({register_1_q, mcu_1_addr}), .b({16{1'b0}}), .eq(comparator_8_eq));  // open: gt, lt
  and and_15 (and_15_out, comparator_8_eq, Breakpoint_D);
  Comparator #(.width(16), .mode("unsigned")) comparator_9 (
    .a({register_1_q, mcu_1_addr}), .b({16{1'b0}}), .eq(comparator_9_eq));  // open: gt, lt
  and and_16 (and_16_out, comparator_9_eq, Breakpoint_E);

  // Notes on the sheet:
  //   Memory Mapped I/O Port Address
  //   Memory Mapped I/O Port Address
  //   Memory Mapped I/O Port Address
  //   PROGRAM MEMORY
  //   Output:
  //   contents of rom_1 (hex, n*v repeats v):
  //   47 ff 0 a0 8f 87 ab 20 d7 83 c 80 c0 e0 4b 1 1 10 8f 7 43 18 93 43 3 84 43 8 90 83 0 a3 67 0 a 21 65
  //   6d 6f 63 6c 65 57 90 83 62 83 98 47 20 0 a0 a3 c4 30 47 80 fc 8f a3 a7 db 83 3c 9b 43 8 e7 83 56 ab
  //   bf ab f2 43 6e f7 83 98 43 a db 83 71 83 36 43 20 f7 83 36 ab 43 1 10 de 83 36 a3 84 20 43 fc 9f a3
  //   d7 83 6f 9b 83 68 48 80 43 20 93 10 5e 93 43 1 9f e0 7 43 10 9f 97 20 d7 83 a1 43 18 93 43 1 84 43 8
  //   90 83 0 a3 43 11 9f 97 20 d7 83 30 4b 0 20 24 90 83 62 83 30 43 1 9f b7 52 9f a7 af 82 f0 10 4c e7
  //   83 b4 3 66 83 ad 47 3f 1 a0 8f 4c 93 e0 3 e7 83 c4 3 66 83 bd 4f 1 1 10 0 a0 8f 7 83 98 50*0 47 ff 0
  //   a0 8f 87 ab 80 43 3 9f e0 7 a3 80 43 3 9f a7 52 9f 97 83 0 0 47 1d 1 a0 8f f0 33 90 83 b4 a3 20 d7
  //   83 34 47 2a 1 a0 8f f0 23 90 83 cc 83 f 47 10 1 a0 8f f0 1b 90 83 b4 a3 20 d7 83 5a 47 17 1 a0 8f f0
  //   17 90 83 cc 83 f 53 0 a 72 61 62 90 83 cc 83 f 5f 0 a 72 61 65 6c 63 6 90 83 b4 a3 20 d7 83 72 47 c
  //   fc 8f 8b 83 f 57 0 a 74 65 73 4 90 83 b4 a3 20 d7 83 8e 53 0 11 0 10 0 a0 8f 8b 8f 8b 83 f 5f 0 a 74
  //   6e 69 72 70 6 90 83 b4 a3 20 d7 83 f 4b 0 3f 1 a0 8f f0 3 a3 52 46 83 af 3 83 a9 90 83 cc 83 f 47 f
  //   0 a0 8f a3 9b 43 18 93 43 2 84 43 8 90 83 0 a3 43 f 9f 97 80 47 fc 0 a0 8f a3 84 20 a3 d7 83 db 9b
  //   83 d4 48 80 35*0 47 ff 0 a0 8f 87 ab 80 43 5 9f e0 7 a3 80 43 5 9f a7 52 9f 97 83 0 43 1 9f b7 52 9f
  //   a7 af a3 30 df 83 27 83 32 c8 a3 c7 83 38 a7 f2 bf db 83 28 a3 c7 83 3a 83 32 43 1 93 83 f 195*0 47
  //   ff 0 a0 8f 87 ab 80 43 8 9f e0 7 a3 80 43 8 9f a7 52 9f 97 83 0 e0 63 5 70 69 6e 67 a 0 10 1 a0 8f
  //   1b 5b 70 6f 6e 67 a 0 17 8f 17 77 b 74 65 73 74 69 6e 67 31 32 33 a 0 1d 8f 33 67 68 6f 6f 72 61 79
  //   21 a 0 2a 8f 23 43 0 a0 83 f
  //    ← Keyboard
  //   Address A
  //   Address B
  //   Address C
  //   Address D
  //   Address E
endmodule

module MCU (
  input  IO_ENABLE,
  input  [7:0] IN,
  input  CLK,
  input  RST,
  output IO_ACTIVE,
  output WRITE_ACTIVE,
  output [7:0] OUT,
  output [7:0] SEG,
  output [7:0] ADDR
);

  wire alu_1_flag, and_1_out, and_2_out, isd_1_address_mux, isd_1_alu_state, isd_1_gpr_forward_input,
       isd_1_memory_select, isd_1_pop, isd_1_push;
  wire [1:0] isd_1_a__r, isd_1_b__r, isd_1_branch, isd_1_c__w, isd_1_gpr_mux;
  wire [2:0] isd_1_alu_op;
  wire [3:0] isd_1_dynamic_op;
  wire [7:0] gpr_1_read_a_2, gpr_1_read_b_2, isd_1_mem_pointer, multiplexer_2_out, multiplexer_3_out,
       pc_1_address, pc_1_address_2, ram_1_data, stk_1_output;

  STK stk_1 (.OUTPUT(stk_1_output), .INPUT(OUT), .CLK(CLK), .POP(isd_1_pop), .PUSH(isd_1_push), .RST(RST));
  PC pc_1 (
    .DATA(multiplexer_3_out), .Jump_Enable(isd_1_branch), .ADDRESS(pc_1_address), .RST(RST),
    .ADDRESS_2(pc_1_address_2), .CLK_Enable(isd_1_address_mux), .CLK(CLK), .ALU(OUT));
  Multiplexer #(.width(8), .enable("false")) multiplexer_1 (
    .in0(pc_1_address), .in1(isd_1_mem_pointer), .out(ADDR), .sel(isd_1_address_mux));
  Multiplexer #(.select(2), .width(8), .enable("false")) multiplexer_2 (
    .in0(OUT), .in1(multiplexer_3_out), .in2(stk_1_output), .in3(pc_1_address_2), .out(multiplexer_2_out),
    .sel(isd_1_gpr_mux));
  ALU alu_1 (
    .OUTPUT(OUT), .OPCODE(isd_1_alu_op), .Input_B(gpr_1_read_b_2), .Input_A(gpr_1_read_a_2),
    .FLAG(alu_1_flag), .DYN_OP(isd_1_dynamic_op), .STATE(isd_1_alu_state));
  GPR gpr_1 (
    .Input(multiplexer_2_out), .Read_B_2(gpr_1_read_b_2), .Read_A_2(gpr_1_read_a_2), .Read_B(isd_1_b__r),
    .Read_A(isd_1_a__r), .CLK(CLK), .RST(RST), .Forward_Input_B(isd_1_gpr_forward_input), .Write(isd_1_c__w));
  ISD isd_1 (
    .DATA(multiplexer_3_out), .CLK(CLK), .RST(RST), .ALU_OP(isd_1_alu_op), .GPR_MUX(isd_1_gpr_mux),
    .Address_MUX(isd_1_address_mux), .POP(isd_1_pop), .PUSH(isd_1_push), .A__R(isd_1_a__r),
    .B__R(isd_1_b__r), .C__W(isd_1_c__w), .Write_Enable(WRITE_ACTIVE), .BRANCH(isd_1_branch),
    .ALU_OUTPUT(OUT), .MEM_POINTER(isd_1_mem_pointer), .Dynamic_OP(isd_1_dynamic_op),
    .ALU_State(isd_1_alu_state), .Memory_Select(isd_1_memory_select), .External_Address_Select(IO_ACTIVE),
    .GPR_Forward_Input(isd_1_gpr_forward_input), .MEM_SEGMENT(SEG), .JMP(alu_1_flag));
  and and_1 (and_1_out, WRITE_ACTIVE, CLK);
  RAM #(.addrWidth(16), .bus("separate")) ram_1 (
    .addr({SEG, ADDR}), .din(OUT), .data(ram_1_data), .sel(1'b1), .clk(and_1_out), .clr(RST));  // open: str, ld
  Multiplexer #(.width(8), .enable("false")) multiplexer_3 (
    .in0(ram_1_data), .in1(IN), .out(multiplexer_3_out), .sel(and_2_out));
  and and_2 (and_2_out, ~isd_1_memory_select, IO_ENABLE);  // AND_Gate

  // Notes on the sheet:
  //   IO_ENABLE: pull=down
  //   OUT: pull=down
  //   IN: pull=down
  //   ADDR: pull=down
  //   RST: pull=down
  //   CLK: pull=down
  //   2 PC Address Bus ------------------------------->
  //   3 PC Output Bus ------->
  //   1 Stack Output Bus ----------------->
  //   4 Memory Pointer Bus -------------->
  //   TISCv2.4
  //   9 Internal Input Bus
  //   <------------------- 7 Register Input Bus
  //   <--------------------------------------------- 8 Memory Output Bus
  //   6 External Input Bus
  //   0 ALU Output Bus
  //   10 Memory Segment Bus
  //   5 Address Bus
endmodule

module ALU (
  input  [7:0] Input_B,
  input  [7:0] Input_A,
  input  STATE,
  input  [2:0] OPCODE,
  input  [3:0] DYN_OP,
  output [7:0] OUTPUT,
  output FLAG
);

  wire _1, and_1_out, and_2_out, and_3_out, and_4_out, and_5_out, and_6_out, and_7_out, and_8_out, and_9_out,
       and_10_out, and_11_out, and_12_out, and_13_out, and_14_out, and_15_out, and_16_out, and_17_out,
       and_18_out, and_19_out, and_20_out, and_21_out, and_22_out, and_23_out, and_24_out, and_25_out,
       and_26_out, and_27_out, and_28_out, and_29_out, and_30_out, and_31_out, and_32_out, and_33_out, CC,
       CI, comparator_1_lt, comparator_2_gt, FC, nA, nB, nor_1_out, nor_2_out, nor_3_out, nor_4_out,
       nor_5_out, nor_6_out, nor_7_out, nor_8_out, not_1_out, o0, o1, o2, o3, o4, o5, o6, o7, OR, or_1_out,
       or_2_out, or_3_out, or_4_out, or_5_out, or_6_out, or_7_out, or_8_out, or_9_out, or_10_out, or_11_out,
       or_12_out, or_13_out, or_14_out, or_15_out, or_16_out, or_17_out, or_18_out, or_19_out, or_20_out,
       or_21_out, or_22_out, or_23_out, or_24_out, or_25_out, or_26_out, or_27_out, xor_1_out, xor_2_out,
       xor_3_out, xor_4_out, xor_5_out, xor_6_out, xor_7_out, xor_8_out, xor_9_out, xor_10_out, xor_11_out,
       xor_12_out, xor_13_out, xor_14_out, xor_15_out, xor_16_out;
  wire [1:0] multiplexer_4_out;
  wire [2:0] bitselector_1_out, multiplexer_3_out, rom_1_data;
  wire [3:0] bitadder_1_out, bitadder_2_out, bitadder_3_out, bitadder_4_out;
  wire [7:0] bit_extender_1_out, multiplexer_5_out, multiplexer_6_out, multiplexer_7_out, multiplexer_8_out,
       shifter_1_out, shifter_2_out;
  wire [7:3] rom_1_data_2;
  wire [8:7] rom_2_data;

  or or_1 (or_1_out, _1, Input_B[0]);
  xor xor_1 (xor_1_out, or_1_out, nB);
  xor xor_2 (xor_2_out, Input_A[0], nA);
  xor xor_3 (xor_3_out, Input_B[1], nB);
  xor xor_4 (xor_4_out, Input_A[1], nA);
  xor xor_5 (xor_5_out, Input_B[2], nB);
  xor xor_6 (xor_6_out, Input_A[2], nA);
  xor xor_7 (xor_7_out, Input_B[3], nB);
  xor xor_8 (xor_8_out, Input_A[3], nA);
  xor xor_9 (xor_9_out, Input_B[4], nB);
  xor xor_10 (xor_10_out, Input_A[4], nA);
  xor xor_11 (xor_11_out, Input_B[5], nB);
  xor xor_12 (xor_12_out, Input_A[5], nA);
  xor xor_13 (xor_13_out, Input_B[6], nB);
  xor xor_14 (xor_14_out, Input_A[6], nA);
  xor xor_15 (xor_15_out, Input_B[7], nB);
  xor xor_16 (xor_16_out, Input_A[7], nA);
  nor nor_1 (nor_1_out, xor_1_out, xor_2_out);
  or or_2 (or_2_out, nor_1_out, and_2_out);
  and and_1 (and_1_out, xor_1_out, xor_2_out);
  and and_2 (and_2_out, and_1_out, ~OR);  // AND_Gate
  and and_3 (and_3_out, and_2_out, ~CC);  // AND_Gate
  or or_3 (or_3_out, and_25_out, FC);
  or or_4 (or_4_out, and_3_out, or_3_out);
  nor nor_2 (nor_2_out, xor_3_out, xor_4_out);
  or or_5 (or_5_out, nor_2_out, and_5_out);
  and and_4 (and_4_out, xor_3_out, xor_4_out);
  and and_5 (and_5_out, and_4_out, ~OR);  // AND_Gate
  and and_6 (and_6_out, and_5_out, ~CC);  // AND_Gate
  or or_6 (or_6_out, and_26_out, FC);
  or or_7 (or_7_out, and_6_out, or_6_out);
  nor nor_3 (nor_3_out, xor_5_out, xor_6_out);
  or or_8 (or_8_out, nor_3_out, and_8_out);
  and and_7 (and_7_out, xor_5_out, xor_6_out);
  and and_8 (and_8_out, and_7_out, ~OR);  // AND_Gate
  and and_9 (and_9_out, and_8_out, ~CC);  // AND_Gate
  or or_9 (or_9_out, and_27_out, FC);
  or or_10 (or_10_out, and_9_out, or_9_out);
  nor nor_4 (nor_4_out, xor_7_out, xor_8_out);
  or or_11 (or_11_out, nor_4_out, and_11_out);
  and and_10 (and_10_out, xor_7_out, xor_8_out);
  and and_11 (and_11_out, and_10_out, ~OR);  // AND_Gate
  or or_12 (or_12_out, and_28_out, FC);
  and and_12 (and_12_out, and_11_out, ~CC);  // AND_Gate
  or or_13 (or_13_out, and_12_out, or_12_out);
  nor nor_5 (nor_5_out, xor_9_out, xor_10_out);
  or or_14 (or_14_out, nor_5_out, and_14_out);
  and and_13 (and_13_out, xor_9_out, xor_10_out);
  and and_14 (and_14_out, and_13_out, ~OR);  // AND_Gate
  and and_15 (and_15_out, and_14_out, ~CC);  // AND_Gate
  or or_15 (or_15_out, and_29_out, FC);
  or or_16 (or_16_out, and_15_out, or_15_out);
  nor nor_6 (nor_6_out, xor_11_out, xor_12_out);
  or or_17 (or_17_out, nor_6_out, and_17_out);
  and and_16 (and_16_out, xor_11_out, xor_12_out);
  and and_17 (and_17_out, and_16_out, ~OR);  // AND_Gate
  and and_18 (and_18_out, and_17_out, ~CC);  // AND_Gate
  or or_18 (or_18_out, and_30_out, FC);
  or or_19 (or_19_out, and_18_out, or_18_out);
  nor nor_7 (nor_7_out, xor_13_out, xor_14_out);
  or or_20 (or_20_out, nor_7_out, and_20_out);
  and and_19 (and_19_out, xor_13_out, xor_14_out);
  and and_20 (and_20_out, and_19_out, ~OR);  // AND_Gate
  or or_21 (or_21_out, and_31_out, FC);
  and and_21 (and_21_out, and_20_out, ~CC);  // AND_Gate
  or or_22 (or_22_out, and_21_out, or_21_out);
  nor nor_8 (nor_8_out, xor_15_out, xor_16_out);
  or or_23 (or_23_out, nor_8_out, and_23_out);
  and and_22 (and_22_out, xor_15_out, xor_16_out);
  and and_23 (and_23_out, and_22_out, ~OR);  // AND_Gate
  or or_24 (or_24_out, and_32_out, FC);
  and and_24 (and_24_out, and_23_out, ~CC);  // AND_Gate
  or or_25 (or_25_out, and_24_out, or_24_out);
  xnor xnor_1 (o0, CI, or_2_out);
  and and_25 (and_25_out, CI, ~or_2_out);  // AND_Gate
  xnor xnor_2 (o1, or_4_out, or_5_out);
  and and_26 (and_26_out, or_4_out, ~or_5_out);  // AND_Gate
  xnor xnor_3 (o2, or_7_out, or_8_out);
  and and_27 (and_27_out, or_7_out, ~or_8_out);  // AND_Gate
  xnor xnor_4 (o3, or_10_out, or_11_out);
  and and_28 (and_28_out, or_10_out, ~or_11_out);  // AND_Gate
  xnor xnor_5 (o4, or_13_out, or_14_out);
  and and_29 (and_29_out, or_13_out, ~or_14_out);  // AND_Gate
  xnor xnor_6 (o5, or_16_out, or_17_out);
  and and_30 (and_30_out, or_16_out, ~or_17_out);  // AND_Gate
  xnor xnor_7 (o6, or_19_out, or_20_out);
  and and_31 (and_31_out, or_19_out, ~or_20_out);  // AND_Gate
  xnor xnor_8 (o7, or_22_out, or_23_out);
  and and_32 (and_32_out, or_22_out, ~or_23_out);  // AND_Gate
  Multiplexer #(.select(2), .enable("false")) multiplexer_1 (
    .in0(or_25_out), .in1(or_26_out), .in2(comparator_2_gt), .in3(comparator_1_lt), .out(FLAG),
    .sel(multiplexer_4_out));
  Multiplexer #(.width(8), .enable("false")) multiplexer_2 (
    .in0({o7, o6, o5, o4, o3, o2, o1, o0}), .in1(multiplexer_8_out), .out(OUTPUT), .sel(and_33_out));
  and and_33 (and_33_out, STATE, or_27_out);
  Multiplexer #(.width(3), .enable("false")) multiplexer_3 (
    .in0(OPCODE), .in1(rom_1_data), .out(multiplexer_3_out), .sel(STATE));
  ROM #(.addrWidth(4)) rom_1 (.addr(DYN_OP), .data({rom_1_data_2, rom_1_data}));  // open: sel
  not not_1 (not_1_out, STATE);
  ROM #(.addrWidth(3), .dataWidth(9)) rom_2 (
    .addr(multiplexer_3_out), .data({rom_2_data, _1, nA, nB, OR, CC, CI, FC}), .sel(1'b1));
  Multiplexer #(.width(2), .enable("false")) multiplexer_4 (
    .in0(rom_1_data_2[4:3]), .in1(rom_2_data), .out(multiplexer_4_out), .sel(not_1_out));
  Multiplexer #(.width(8), .enable("false")) multiplexer_5 (
    .in0({8{1'b0}}), .in1(Input_A), .out(multiplexer_5_out), .sel(or_27_out));
  BitSelector #(.group(3)) bitselector_1 (.in(multiplexer_6_out), .out(bitselector_1_out), .sel(2'b00));
  Multiplexer #(.width(8), .enable("false")) multiplexer_6 (
    .in0({8{1'b0}}), .in1(Input_B), .out(multiplexer_6_out), .sel(or_27_out));
  Multiplexer #(.width(8), .enable("false")) multiplexer_7 (
    .in0({8{1'b0}}), .in1({o7, o6, o5, o4, o3, o2, o1, o0}), .out(multiplexer_7_out), .sel(or_27_out));
  BitAdder bitadder_1 (.in0(multiplexer_6_out), .out(bitadder_1_out));
  BitAdder bitadder_2 (.in0(multiplexer_5_out), .out(bitadder_2_out));
  Shifter shifter_1 (.in(multiplexer_5_out), .\dist (bitselector_1_out), .out(shifter_1_out));
  Shifter #(.shift("lr")) shifter_2 (.in(multiplexer_5_out), .\dist (bitselector_1_out), .out(shifter_2_out));
  assign bit_extender_1_out = {{4{1'b0}}, bitadder_3_out};  // Bit_Extender bit_extender_1
  BitAdder bitadder_3 (.in0(multiplexer_7_out), .out(bitadder_3_out));
  or or_26 (or_26_out, o0, o1, o2, o3, o4, o5, o6, o7);
  or or_27 (or_27_out, rom_1_data_2[5], rom_1_data_2[6], rom_1_data_2[7]);
  Multiplexer #(.select(2), .width(8), .enable("false")) multiplexer_8 (
    .in0(shifter_1_out), .in1(shifter_2_out), .in2(bit_extender_1_out), .in3({8{1'b0}}),
    .out(multiplexer_8_out), .sel(rom_1_data_2[7:6]));
  Comparator #(.width(4)) comparator_1 (.a(bitadder_1_out), .b(bitadder_2_out), .lt(comparator_1_lt));  // open: gt, eq
  Comparator #(.width(4)) comparator_2 (.a(bitadder_2_out), .b(bitadder_4_out), .gt(comparator_2_gt));  // open: eq, lt
  BitAdder bitadder_4 (.in0(multiplexer_8_out), .out(bitadder_4_out));

  // Other names for the same wires on the sheet: A[7:0] = Input_A; a0 = Input_A[0]; a1 = Input_A[1]; a2 = Input_A[2];
  //   a3 = Input_A[3]; a4 = Input_A[4]; a5 = Input_A[5]; a6 = Input_A[6]; a7 = Input_A[7]; B[7:0] = Input_B;
  //   b0 = Input_B[0]; b1 = Input_B[1]; b2 = Input_B[2]; b3 = Input_B[3]; b4 = Input_B[4]; b5 = Input_B[5];
  //   b6 = Input_B[6]; b7 = Input_B[7]

  // Notes on the sheet:
  //   Opcodes
  //   contents of rom_1 (hex, n*v repeats v):
  //   3 7 9 a 80 4 30 50
  //   contents of rom_2 (hex, n*v repeats v):
  //   88 bb 84 0 2 b8 52 12
  //   OPCODES: 000: OR, 001: AND, 010: XOR, 011: ADD, 100: CIN, 101: NAND, 110: DECR, 111: SUB
endmodule

module GPR (
  input  [7:0] Input,
  input  [1:0] Write,
  input  CLK,
  input  RST,
  input  Forward_Input_B,
  input  [1:0] Read_B,
  input  [1:0] Read_A,
  output [7:0] Read_B_2,
  output [7:0] Read_A_2
);

  wire decoder_1_out1, decoder_1_out2, decoder_1_out3;
  wire [7:0] multiplexer_3_out, register_1_q, register_2_q, register_3_q;

  Decoder #(.select(2), .enable("false")) decoder_1 (
    .out1(decoder_1_out1), .out2(decoder_1_out2), .out3(decoder_1_out3), .sel(Write));  // open: out0
  Multiplexer #(.select(2), .width(8), .enable("false")) multiplexer_1 (
    .in0(multiplexer_3_out), .in1(register_1_q), .in2(register_2_q), .in3(register_3_q), .out(Read_B_2),
    .sel(Read_B));
  Multiplexer #(.select(2), .width(8), .enable("false")) multiplexer_2 (
    .in0({8{1'b0}}), .in1(register_1_q), .in2(register_2_q), .in3(register_3_q), .out(Read_A_2), .sel(Read_A));
  Register register_1 (.D(Input), .en(decoder_1_out1), .Q(register_1_q), .clk(CLK), .clr(RST));
  Register register_2 (.D(Input), .en(decoder_1_out2), .Q(register_2_q), .clk(CLK), .clr(RST));
  Register register_3 (.D(Input), .en(decoder_1_out3), .Q(register_3_q), .clk(CLK), .clr(RST));
  Multiplexer #(.width(8), .enable("false")) multiplexer_3 (
    .in0({8{1'b0}}), .in1(Input), .out(multiplexer_3_out), .sel(Forward_Input_B));
endmodule

module ISD (
  input  [7:0] DATA,
  input  CLK,
  input  RST,
  input  [7:0] ALU_OUTPUT,
  input  JMP,
  output Write_Enable,
  output ALU_State,
  output GPR_Forward_Input,
  output POP,
  output PUSH,
  output [2:0] ALU_OP,
  output [1:0] GPR_MUX,
  output [1:0] A__R,
  output [1:0] B__R,
  output [1:0] C__W,
  output [7:0] MEM_SEGMENT,
  output [7:0] MEM_POINTER,
  output [3:0] Dynamic_OP,
  output External_Address_Select,
  output [1:0] BRANCH,
  output Memory_Select,
  output Address_MUX
);

  wire and_1_out, AND_2_out, and_3_out, and_4_out, and_5_out, and_6_out, and_8_out, and_9_out, and_10_out,
       and_12_out, and_14_out, and_16_out, and_17_out, and_18_out, and_19_out, and_20_out, and_21_out,
       and_22_out, and_23_out, and_24_out, CMP_out, comparator_1_gt, comparator_2_lt, comparator_3_eq,
       comparator_3_gt, comparator_4_lt, comparator_5_eq, comparator_6_lt, comparator_7_eq, DECR_out,
       INCR_out, JMP_out, LB_out, LNI_LI_out, mnb_decr_out, mnb_incr_out, mnb_load_out, mnb_noincr_out,
       MNB_out, mnb_store_out, nand_2_out, NAND_out, not_1_out, ONE_out, OP_out, or_1_out, or_2_out,
       or_3_out, or_4_out, or_5_out, or_6_out, or_7_out, or_8_out, or_9_out, or_10_out, OR_11_out, or_12_out,
       or_13_out, or_14_out, or_16_out, or_17_out, or_18_out, or_19_out, or_20_out, or_21_out, or_24_out,
       or_25_out, or_26_out, or_27_out, or_28_out, or_29_out, or_30_out, or_31_out, or_32_out, or_33_out,
       or_34_out, or_35_out, or_36_out, or_37_out, or_38_out, or_39_out, or_40_out, or_41_out, or_42_out,
       or_43_out, or_44_out, or_45_out, or_46_out, or_47_out, or_48_out, or_49_out, or_50_out, or_51_out,
       or_52_out, or_53_out, or_54_out, or_56_out, or_57_out, or_58_out, or_61_out, or_62_out, or_63_out,
       or_64_out, or_65_out, or_66_out, or_67_out, or_68_out, or_69_out, or_70_out, or_72_out, or_73_out,
       or_74_out, or_75_out, or_77_out, or_78_out, or_79_out, or_80_out, or_81_out, or_84_out, or_85_out,
       or_86_out, or_87_out, or_88_out, or_89_out, or_91_out, or_92_out, or_93_out, or_94_out, or_95_out,
       or_98_out, or_99_out, or_100_out, or_101_out, or_102_out, or_103_out, pcr_out, PEEK_out, POP_out,
       PTRADD_out, PUSH_out, register_4_q, register_5_q, register_6_q, register_7_q, register_11_q,
       register_12_q, register_13_q, register_14_q, register_15_q, SB_out, seg_out, SOP_out, SP_out, XOR_out;
  wire [1:0] multiplexer_3_out, multiplexer_4_out, multiplexer_5_out, or_83_out;
  wire [1:1] or_82_out;
  wire [3:0] multiplexer_1_out_2;
  wire [4:0] adder_2_out, bit_extender_1_out, multiplexer_10_out, multiplexer_11_out, register_8_q,
       register_9_q, subtractor_1_out, subtractor_2_out;
  wire [7:0] adder_1_out, multiplexer_1_out, multiplexer_2_out, multiplexer_6_out, register_1_q;

  not not_1 (not_1_out, or_85_out);
  Register #(.trigger("falling")) register_1 (.D(DATA), .en(not_1_out), .Q(register_1_q), .clk(CLK), .clr(RST));
  Multiplexer #(.width(8), .enable("false")) multiplexer_1 (
    .in0(register_1_q), .in1({8{1'b0}}),
    .out({multiplexer_1_out[7:6], multiplexer_1_out_2, multiplexer_1_out[1:0]}), .sel(or_84_out));
  or or_1 (or_1_out, multiplexer_1_out_2[0], multiplexer_1_out_2[1]);
  or or_2 (or_2_out, multiplexer_1_out_2[0], multiplexer_1_out_2[1]);
  or or_3 (or_3_out, multiplexer_1_out_2[2], multiplexer_1_out_2[3]);
  or or_4 (or_4_out, multiplexer_1_out_2[2], multiplexer_1_out_2[3]);
  or or_5 (or_5_out, multiplexer_1_out_2[0], multiplexer_1_out_2[1]);
  or or_6 (or_6_out, multiplexer_1_out_2[0], multiplexer_1_out_2[1]);
  or or_7 (or_7_out, multiplexer_1_out_2[2], multiplexer_1_out_2[3]);
  or or_8 (or_8_out, multiplexer_1_out_2[0], multiplexer_1_out_2[1]);
  or or_9 (or_9_out, multiplexer_1_out_2[2], multiplexer_1_out_2[3]);
  and and_1 (and_1_out, ~multiplexer_1_out_2[2], ~multiplexer_1_out_2[3]);  // AND_Gate
  Register register_2 (.D(ALU_OUTPUT), .en(seg_out), .Q(MEM_SEGMENT), .clk(CLK), .clr(RST));
  Register register_3 (.D(multiplexer_2_out), .en(or_10_out), .Q(MEM_POINTER), .clk(CLK), .clr(RST));
  Multiplexer #(.width(8), .enable("false")) multiplexer_2 (
    .in0(ALU_OUTPUT), .in1(adder_1_out), .out(multiplexer_2_out), .sel(and_6_out));
  or or_10 (or_10_out, and_6_out, or_75_out);
  and SOP (SOP_out, ~multiplexer_1_out[0], ~multiplexer_1_out[1], ~multiplexer_1_out_2[0], ~multiplexer_1_out_2[1], 1'b1, 1'b1, 1'b1, 1'b1);  // AND_Gate
  and OR_11 (OR_11_out, ~multiplexer_1_out[0], ~multiplexer_1_out[1], 1'b1, or_1_out, 1'b1, 1'b1, 1'b1, 1'b1);  // AND_Gate
  and NAND (NAND_out, multiplexer_1_out[0], ~multiplexer_1_out[1], 1'b1, or_2_out, 1'b1, or_3_out, 1'b1, 1'b1);  // AND_Gate
  or or_12 (or_12_out, NAND_out, 1'b0);
  and AND_2 (AND_2_out, multiplexer_1_out[0], ~multiplexer_1_out[1], ~multiplexer_1_out_2[0], ~multiplexer_1_out_2[1], or_4_out, 1'b1, 1'b1, 1'b1);  // AND_Gate
  and XOR (XOR_out, multiplexer_1_out[0], ~multiplexer_1_out[1], 1'b1, or_5_out, ~multiplexer_1_out_2[2], ~multiplexer_1_out_2[3], 1'b1, 1'b1);  // AND_Gate
  and PTRADD (PTRADD_out, multiplexer_1_out[0], ~multiplexer_1_out[1], ~multiplexer_1_out_2[0], ~multiplexer_1_out_2[1], ~multiplexer_1_out_2[2], ~multiplexer_1_out_2[3], 1'b1, 1'b1);  // AND_Gate
  and DECR (DECR_out, ~multiplexer_1_out[0], multiplexer_1_out[1], 1'b1, or_6_out, ~multiplexer_1_out_2[2], ~multiplexer_1_out_2[3], 1'b1, 1'b1);  // AND_Gate
  or or_13 (or_13_out, DECR_out, or_12_out);
  and INCR (INCR_out, ~multiplexer_1_out[0], multiplexer_1_out[1], ~multiplexer_1_out_2[0], ~multiplexer_1_out_2[1], or_7_out, 1'b1, 1'b1, 1'b1);  // AND_Gate
  or or_14 (or_14_out, INCR_out, or_13_out);
  and ONE (ONE_out, ~multiplexer_1_out[0], multiplexer_1_out[1], ~multiplexer_1_out_2[0], ~multiplexer_1_out_2[1], ~multiplexer_1_out_2[2], ~multiplexer_1_out_2[3], 1'b1, 1'b1);  // AND_Gate
  or or_15 (ALU_OP[2], ONE_out, or_14_out);
  and OP (OP_out, ~multiplexer_1_out[0], multiplexer_1_out[1], 1'b1, or_8_out, 1'b1, or_9_out, 1'b1, 1'b1);  // AND_Gate
  and MNB (MNB_out, multiplexer_1_out[0], multiplexer_1_out[1], 1'b1, 1'b1, 1'b1, 1'b1, ~multiplexer_1_out[6], ~multiplexer_1_out[7]);  // AND_Gate
  and LNI_LI (LNI_LI_out, multiplexer_1_out[0], multiplexer_1_out[1], 1'b1, 1'b1, 1'b1, 1'b1, multiplexer_1_out[6], ~multiplexer_1_out[7]);  // AND_Gate
  and u_JMP (JMP_out, multiplexer_1_out[0], multiplexer_1_out[1], ~multiplexer_1_out_2[0], ~multiplexer_1_out_2[1], ~multiplexer_1_out_2[2], ~multiplexer_1_out_2[3], ~multiplexer_1_out[6], multiplexer_1_out[7]);  // AND_Gate
  and u_PUSH (PUSH_out, multiplexer_1_out[0], multiplexer_1_out[1], ~multiplexer_1_out_2[0], ~multiplexer_1_out_2[1], multiplexer_1_out_2[2], ~multiplexer_1_out_2[3], ~multiplexer_1_out[6], multiplexer_1_out[7]);  // AND_Gate
  and u_POP (POP_out, multiplexer_1_out[0], multiplexer_1_out[1], ~multiplexer_1_out_2[0], ~multiplexer_1_out_2[1], ~multiplexer_1_out_2[2], multiplexer_1_out_2[3], ~multiplexer_1_out[6], multiplexer_1_out[7]);  // AND_Gate
  and PEEK (PEEK_out, multiplexer_1_out[0], multiplexer_1_out[1], ~multiplexer_1_out_2[0], ~multiplexer_1_out_2[1], multiplexer_1_out_2[2], multiplexer_1_out_2[3], ~multiplexer_1_out[6], multiplexer_1_out[7]);  // AND_Gate
  and LB (LB_out, multiplexer_1_out[0], multiplexer_1_out[1], multiplexer_1_out_2[0], ~multiplexer_1_out_2[1], 1'b1, 1'b1, ~multiplexer_1_out[6], multiplexer_1_out[7]);  // AND_Gate
  and SB (SB_out, multiplexer_1_out[0], multiplexer_1_out[1], ~multiplexer_1_out_2[0], multiplexer_1_out_2[1], 1'b1, 1'b1, ~multiplexer_1_out[6], multiplexer_1_out[7]);  // AND_Gate
  and SP (SP_out, multiplexer_1_out[0], multiplexer_1_out[1], multiplexer_1_out_2[0], multiplexer_1_out_2[1], 1'b1, 1'b1, ~multiplexer_1_out[6], multiplexer_1_out[7]);  // AND_Gate
  and CMP (CMP_out, multiplexer_1_out[0], multiplexer_1_out[1], 1'b1, 1'b1, 1'b1, 1'b1, multiplexer_1_out[6], multiplexer_1_out[7]);
  Multiplexer #(.width(2), .enable("false")) multiplexer_3 (
    .in0(2'b00), .in1(multiplexer_1_out_2[1:0]), .out(multiplexer_3_out), .sel(or_40_out));
  Multiplexer #(.width(2), .enable("false")) multiplexer_4 (
    .in0(2'b00), .in1(multiplexer_1_out_2[3:2]), .out(multiplexer_4_out), .sel(or_39_out));
  Multiplexer #(.width(2), .enable("false")) multiplexer_5 (
    .in0(2'b00), .in1(multiplexer_1_out[7:6]), .out(multiplexer_5_out), .sel(or_50_out));
  or or_16 (or_16_out, NAND_out, 1'b0);
  or or_17 (or_17_out, AND_2_out, or_16_out);
  or or_18 (or_18_out, XOR_out, 1'b0);
  or or_19 (or_19_out, PTRADD_out, or_18_out);
  or or_20 (or_20_out, PTRADD_out, or_17_out);
  or or_21 (or_21_out, DECR_out, or_19_out);
  or or_22 (ALU_OP[0], OP_out, or_20_out);
  or or_23 (ALU_OP[1], OP_out, or_21_out);
  and and_3 (and_3_out, and_1_out, LB_out);
  and and_4 (and_4_out, and_1_out, SB_out);
  and and_5 (and_5_out, and_1_out, SP_out);
  Multiplexer #(.width(8), .enable("false")) multiplexer_6 (
    .in0(8'h1), .in1({8{1'b1}}), .out(multiplexer_6_out), .sel(register_14_q));
  Comparator #(.width(16), .mode("unsigned")) comparator_1 (
    .a({MEM_SEGMENT, MEM_POINTER}), .b(16'hff), .gt(comparator_1_gt));  // open: eq, lt
  Comparator #(.width(16), .mode("unsigned")) comparator_2 (
    .a({MEM_SEGMENT, MEM_POINTER}), .b(16'hfc), .lt(comparator_2_lt));  // open: gt, eq
  or or_24 (or_24_out, OR_11_out, 1'b0);
  or or_25 (or_25_out, OR_11_out, 1'b0);
  or or_26 (or_26_out, NAND_out, or_24_out);
  or or_27 (or_27_out, NAND_out, or_25_out);
  or or_28 (or_28_out, AND_2_out, or_27_out);
  or or_29 (or_29_out, XOR_out, or_26_out);
  or or_30 (or_30_out, PTRADD_out, or_29_out);
  or or_31 (or_31_out, DECR_out, or_30_out);
  or or_32 (or_32_out, INCR_out, or_28_out);
  or or_33 (or_33_out, INCR_out, or_31_out);
  or or_34 (or_34_out, OP_out, or_33_out);
  or or_35 (or_35_out, OP_out, or_32_out);
  or or_36 (or_36_out, LB_out, or_35_out);
  or or_37 (or_37_out, SB_out, or_36_out);
  or or_38 (or_38_out, SP_out, or_37_out);
  or or_39 (or_39_out, CMP_out, or_38_out);
  or or_40 (or_40_out, CMP_out, or_34_out);
  Adder adder_1 (.a(MEM_POINTER), .b(multiplexer_6_out), .out(adder_1_out));  // open: cin, cout
  or or_41 (or_41_out, comparator_1_gt, comparator_2_lt);
  or or_42 (or_42_out, OR_11_out, 1'b0);
  or or_43 (or_43_out, NAND_out, or_42_out);
  or or_44 (or_44_out, AND_2_out, or_43_out);
  or or_45 (or_45_out, XOR_out, or_44_out);
  or or_46 (or_46_out, PTRADD_out, or_45_out);
  or or_47 (or_47_out, DECR_out, or_46_out);
  or or_48 (or_48_out, INCR_out, or_47_out);
  or or_49 (or_49_out, ONE_out, or_48_out);
  or or_50 (or_50_out, OP_out, or_49_out);
  or or_51 (or_51_out, POP_out, and_8_out);
  or or_52 (or_52_out, PEEK_out, or_51_out);
  or or_53 (or_53_out, and_4_out, or_52_out);
  or or_54 (or_54_out, and_5_out, or_53_out);
  or or_55 (GPR_MUX[1], pcr_out, seg_out, or_54_out);
  and and_6 (and_6_out, or_93_out, or_103_out);
  and and_7 (External_Address_Select, ~or_41_out, Address_MUX);  // AND_Gate
  and and_8 (and_8_out, or_93_out, register_15_q);
  and and_9 (and_9_out, or_93_out, ~register_15_q);  // AND_Gate
  or or_56 (or_56_out, LNI_LI_out, or_89_out, and_9_out);
  or or_57 (or_57_out, LB_out, or_56_out);
  or or_58 (or_58_out, LB_out, or_93_out);
  or or_59 (Address_MUX, SB_out, or_58_out);
  or or_60 (GPR_MUX[0], pcr_out, or_57_out);
  and and_10 (and_10_out, or_72_out, JMP);
  and and_11 (Memory_Select, or_41_out, Address_MUX);
  or or_61 (or_61_out, OR_11_out, 1'b0);
  or or_62 (or_62_out, NAND_out, or_61_out);
  or or_63 (or_63_out, AND_2_out, or_62_out);
  or or_64 (or_64_out, XOR_out, or_63_out);
  or or_65 (or_65_out, PTRADD_out, or_64_out);
  or or_66 (or_66_out, DECR_out, or_65_out);
  or or_67 (or_67_out, INCR_out, or_66_out);
  or or_68 (or_68_out, POP_out, and_8_out);
  or or_69 (or_69_out, and_4_out, or_68_out);
  or or_70 (or_70_out, and_5_out, or_69_out);
  or or_71 (POP, seg_out, or_70_out);
  or or_72 (or_72_out, CMP_out, or_67_out);
  Register #(.width(1), .trigger("falling")) register_4 (
    .D(and_10_out), .en(1'b1), .Q(register_4_q), .clk(CLK), .clr(RST));
  and and_12 (and_12_out, ~and_17_out, or_89_out);  // AND_Gate
  or or_73 (or_73_out, and_9_out, PUSH_out, and_12_out);
  or or_74 (or_74_out, and_3_out, or_73_out);
  or or_75 (or_75_out, SP_out, PTRADD_out);
  or or_76 (PUSH, pcr_out, or_74_out);
  Multiplexer #(.select(2), .width(2), .enable("false")) multiplexer_7 (
    .in0(multiplexer_3_out), .in1(2'b01), .in2(multiplexer_5_out), .in3(2'b01), .out(A__R), .sel(or_83_out));
  and and_13 (BRANCH[0], JMP_out, ~register_4_q);  // AND_Gate
  or or_77 (or_77_out, JMP_out, Address_MUX);
  or or_78 (or_78_out, PTRADD_out, 1'b0);
  and and_14 (and_14_out, LNI_LI_out, and_17_out);
  or or_79 (or_79_out, and_14_out, 1'b0);
  or or_80 (or_80_out, PUSH_out, or_78_out);
  or or_81 (or_81_out, POP_out, or_79_out);
  or or_82 (or_82_out[1], PEEK_out, or_81_out);
  or or_83 (or_83_out[0], BRANCH[1], or_80_out);
  and and_15 (or_83_out[1], or_39_out, or_88_out);
  nand nand_2 (nand_2_out, or_88_out, or_40_out);
  Multiplexer #(.width(2), .enable("false")) multiplexer_8 (
    .in0(multiplexer_5_out), .in1(multiplexer_4_out), .out(B__R), .sel(nand_2_out));
  Register #(.width(1), .trigger("falling")) register_5 (
    .D(or_77_out), .Q(register_5_q), .clk(CLK), .clr(RST));  // open: en
  or or_84 (or_84_out, register_5_q, or_93_out, or_95_out);
  or or_85 (or_85_out, or_93_out, or_95_out);
  or or_86 (or_86_out, AND_2_out, 1'b0);
  or or_87 (or_87_out, XOR_out, or_86_out);
  or or_88 (or_88_out, or_75_out, or_87_out);
  Multiplexer #(.select(2), .width(2), .enable("false")) multiplexer_9 (
    .in0(multiplexer_5_out), .in1(B__R), .in2(2'b01), .in3(2'b00), .out(C__W),
    .sel({or_82_out[1], Address_MUX}));
  and seg (seg_out, ~multiplexer_1_out_2[2], multiplexer_1_out_2[3], ~multiplexer_1_out[6], multiplexer_1_out[7], SOP_out);  // AND_Gate
  and pcr (pcr_out, multiplexer_1_out_2[2], ~multiplexer_1_out_2[3], ~multiplexer_1_out[6], multiplexer_1_out[7], SOP_out);  // AND_Gate
  and go (BRANCH[1], ~multiplexer_1_out_2[2], ~multiplexer_1_out_2[3], ~multiplexer_1_out[6], multiplexer_1_out[7], SOP_out);  // AND_Gate
  and and_16 (and_16_out, MNB_out, comparator_3_eq);
  Register #(.width(1)) register_6 (.D(and_16_out), .en(1'b1), .Q(register_6_q), .clk(CLK), .clr(RST));
  or or_89 (or_89_out, LNI_LI_out, and_18_out);
  and and_17 (and_17_out, LNI_LI_out, comparator_3_eq);
  Register #(.width(1)) register_7 (.D(and_17_out), .en(1'b1), .Q(register_7_q), .clk(CLK), .clr(RST));
  or or_90 (ALU_State, OP_out, CMP_out);
  or or_91 (or_91_out, BRANCH[1], pcr_out, seg_out);
  Register #(.width(5)) register_8 (.D(multiplexer_10_out), .en(or_92_out), .Q(register_8_q), .clk(CLK), .clr(RST));
  Multiplexer #(.width(5), .enable("false")) multiplexer_10 (
    .in0(subtractor_1_out), .in1(adder_2_out), .out(multiplexer_10_out), .sel(MNB_out));
  or or_92 (or_92_out, ~comparator_5_eq, MNB_out);  // OR_Gate
  or or_93 (or_93_out, ~comparator_5_eq, register_11_q);  // OR_Gate
  Multiplexer #(.width(5), .enable("false")) multiplexer_11 (
    .in0(subtractor_2_out), .in1(adder_2_out), .out(multiplexer_11_out), .sel(LNI_LI_out));
  Register #(.width(5)) register_9 (.D(multiplexer_11_out), .en(or_94_out), .Q(register_9_q), .clk(CLK), .clr(RST));
  or or_94 (or_94_out, ~comparator_7_eq, LNI_LI_out);  // OR_Gate
  or or_95 (or_95_out, ~comparator_7_eq, register_12_q);  // OR_Gate
  and and_18 (and_18_out, ~comparator_7_eq, ~register_7_q);  // AND_Gate
  Comparator #(.width(4)) comparator_3 (
    .a(multiplexer_1_out_2), .b(4'b0000), .gt(comparator_3_gt), .eq(comparator_3_eq));  // open: lt
  assign bit_extender_1_out = {{1{1'b0}}, multiplexer_1_out_2};  // Bit_Extender bit_extender_1
  and and_19 (and_19_out, register_15_q, or_93_out);
  Register #(.width(4), .trigger("falling")) register_10 (
    .D({multiplexer_1_out[7:6], multiplexer_1_out_2[3:2]}), .en(and_20_out), .Q(Dynamic_OP), .clk(CLK),
    .clr(RST));
  and and_20 (and_20_out, ~or_89_out, ~or_91_out, ~or_98_out, ~or_84_out, SOP_out);  // AND_Gate
  Comparator #(.width(5)) comparator_4 (.a(multiplexer_10_out), .b({5{1'b0}}), .lt(comparator_4_lt));  // open: gt, eq
  Subtractor #(.width(5)) subtractor_1 (.a(register_8_q), .b(5'b00001), .out(subtractor_1_out));  // open: bin, bout
  Comparator #(.width(5)) comparator_5 (.a(register_8_q), .b({5{1'b0}}), .eq(comparator_5_eq));  // open: gt, lt
  Comparator #(.width(5)) comparator_6 (.a(multiplexer_11_out), .b({5{1'b0}}), .lt(comparator_6_lt));  // open: gt, eq
  Subtractor #(.width(5)) subtractor_2 (.a(register_9_q), .b(5'b00001), .out(subtractor_2_out));  // open: bin, bout
  Comparator #(.width(5)) comparator_7 (.a(register_9_q), .b({5{1'b0}}), .eq(comparator_7_eq));  // open: gt, lt
  Adder #(.width(5)) adder_2 (
    .a({5{1'b0}}), .b(bit_extender_1_out), .out(adder_2_out), .cin(comparator_3_eq));  // open: cout
  or or_96 (Write_Enable, and_19_out, SB_out);
  or or_97 (GPR_Forward_Input, and_3_out, and_4_out, and_5_out, seg_out, pcr_out, or_93_out, or_89_out);
  and mnb_noincr (mnb_noincr_out, multiplexer_1_out_2[2], multiplexer_1_out_2[3], ~multiplexer_1_out[6], multiplexer_1_out[7], SOP_out);  // AND_Gate
  and mnb_incr (mnb_incr_out, ~multiplexer_1_out_2[2], ~multiplexer_1_out_2[3], multiplexer_1_out[6], multiplexer_1_out[7], SOP_out);  // AND_Gate
  and mnb_decr (mnb_decr_out, multiplexer_1_out_2[2], ~multiplexer_1_out_2[3], multiplexer_1_out[6], multiplexer_1_out[7], SOP_out);  // AND_Gate
  and mnb_store (mnb_store_out, ~multiplexer_1_out_2[2], multiplexer_1_out_2[3], multiplexer_1_out[6], multiplexer_1_out[7], SOP_out);  // AND_Gate
  and mnb_load (mnb_load_out, multiplexer_1_out_2[2], multiplexer_1_out_2[3], multiplexer_1_out[6], multiplexer_1_out[7], SOP_out);
  or or_98 (or_98_out, or_101_out, or_102_out);
  and and_21 (and_21_out, ~comparator_4_lt, ~and_16_out);  // AND_Gate
  and and_22 (and_22_out, and_21_out, or_99_out, ~register_6_q);  // AND_Gate
  or or_99 (or_99_out, ~comparator_5_eq, comparator_3_gt);  // OR_Gate
  Register #(.width(1)) register_11 (.D(and_22_out), .Q(register_11_q), .clk(CLK), .clr(RST));  // open: en
  and and_23 (and_23_out, ~comparator_6_lt, ~and_17_out);  // AND_Gate
  and and_24 (and_24_out, and_23_out, or_100_out, ~register_7_q);  // AND_Gate
  or or_100 (or_100_out, ~comparator_7_eq, comparator_3_gt);  // OR_Gate
  Register #(.width(1)) register_12 (.D(and_24_out), .en(1'b1), .Q(register_12_q), .clk(CLK), .clr(RST));
  Register #(.width(1), .trigger("falling")) register_13 (
    .D(mnb_incr_out), .en(or_101_out), .Q(register_13_q), .clk(CLK), .clr(RST));
  Register #(.width(1), .trigger("falling")) register_14 (
    .D(mnb_decr_out), .en(or_101_out), .Q(register_14_q), .clk(CLK), .clr(RST));
  or or_101 (or_101_out, mnb_decr_out, mnb_incr_out, mnb_noincr_out);
  Register #(.width(1), .trigger("falling")) register_15 (
    .D(mnb_store_out), .en(or_102_out), .Q(register_15_q), .clk(CLK), .clr(RST));
  or or_102 (or_102_out, mnb_store_out, mnb_load_out);
  or or_103 (or_103_out, register_14_q, register_13_q);

  // Notes on the sheet:
  //   DATA: pull=down
  //   GPR_Forward_Input: pull=down
  //   This input defines the range of MMIO -->
endmodule

module STK (
  input  [7:0] INPUT,
  input  CLK,
  input  RST,
  input  POP,
  input  PUSH,
  output [7:0] OUTPUT
);

  wire or_1_out;
  wire [15:0] adder_1_out, multiplexer_1_out, multiplexer_2_out, register_1_q, subtractor_1_out;

  or or_1 (or_1_out, POP, PUSH);
  Register #(.width(16)) register_1 (.D(multiplexer_2_out), .en(or_1_out), .Q(register_1_q), .clk(CLK), .clr(RST));
  Adder #(.width(16)) adder_1 (.a(register_1_q), .b(16'h1), .out(adder_1_out));  // open: cin, cout
  Subtractor #(.width(16)) subtractor_1 (.a(register_1_q), .b(16'h1), .out(subtractor_1_out));  // open: bin, bout
  Multiplexer #(.width(16), .enable("false")) multiplexer_1 (
    .in0(register_1_q), .in1(multiplexer_2_out), .out(multiplexer_1_out), .sel(PUSH));
  Multiplexer #(.width(16), .enable("false")) multiplexer_2 (
    .in0(adder_1_out), .in1(subtractor_1_out), .out(multiplexer_2_out), .sel(POP));
  RAM #(.addrWidth(16), .bus("separate")) ram_1 (
    .addr(multiplexer_1_out), .din(INPUT), .data(OUTPUT), .str(PUSH), .clk(CLK), .clr(RST));  // open: sel, ld
endmodule

module PC (
  input  [7:0] DATA,
  input  [7:0] ALU,
  input  [1:0] Jump_Enable,
  input  CLK_Enable,
  input  CLK,
  input  RST,
  output [7:0] ADDRESS_2,
  output [7:0] ADDRESS
);

  wire not_1_out;
  wire [7:0] adder_1_out, adder_2_out, multiplexer_1_out, register_1_q;

  Adder adder_1 (.a(ALU), .b(8'h1), .out(adder_1_out));  // open: cin, cout
  Register #(.trigger("falling")) register_1 (
    .D(multiplexer_1_out), .en(not_1_out), .Q(register_1_q), .clk(CLK), .clr(RST));
  Multiplexer #(.select(2), .width(8), .enable("false")) multiplexer_1 (
    .in0(adder_2_out), .in1(DATA), .in2(adder_1_out), .out(multiplexer_1_out), .sel(Jump_Enable));  // open: in3
  not not_1 (not_1_out, CLK_Enable);
  Adder adder_2 (.a(register_1_q), .b(8'h1), .out(adder_2_out));  // open: cin, cout
  Multiplexer #(.width(8), .disabled(0), .enable("false")) multiplexer_2 (
    .in0(register_1_q), .in1(ALU), .out(ADDRESS), .sel(Jump_Enable[1]));
  Adder adder_3 (.a(adder_2_out), .b(8'h1), .out(ADDRESS_2));  // open: cin, cout
endmodule

module AU (
  input  [7:0] INPUT,
  input  CLK,
  input  WRITE_EN,
  input  RST,
  input  READ_EN,
  output [7:0] FPU
);

  wire and_1_out, and_2_out, or_1_out, or_2_out, register_4_q;
  wire [1:0] register_2_q, subtractor_1_out;
  wire [2:0] bitselector_2_out;
  wire [7:0] register_1_q, register_3_q, register_6_q, register_7_q, register_12_q;
  wire [23:0] register_8_q;
  wire [23:16] register_5_q;
  wire [31:0] adder_1_out, divider_1_out, multiplexer_1_out, multiplier_1_out, register_10_q,
       subtractor_2_out;

  Register register_1 (.D(INPUT), .en(WRITE_EN), .Q(register_1_q), .clk(CLK), .clr(RST));
  and and_1 (and_1_out, ~WRITE_EN, READ_EN);  // AND_Gate
  Subtractor #(.width(2)) subtractor_1 (.a(register_2_q), .b(2'b00), .out(subtractor_1_out), .bin(1'b1));  // open: bout
  Register #(.width(2)) register_2 (.D(subtractor_1_out), .en(and_1_out), .Q(register_2_q), .clk(CLK), .clr(or_1_out));
  BitSelector #(.width(32), .group(8)) bitselector_1 (.in(register_10_q), .out(FPU), .sel(subtractor_1_out));
  or or_1 (or_1_out, RST, and_2_out);
  and and_2 (and_2_out, CLK, register_4_q, WRITE_EN);
  Register register_3 (.D(register_1_q), .en(WRITE_EN), .Q(register_3_q), .clk(CLK), .clr(or_1_out));
  Register #(.width(1)) register_4 (.D(or_2_out), .en(WRITE_EN), .Q(register_4_q), .clk(CLK), .clr(or_1_out));
  Register register_5 (.D(register_3_q), .en(WRITE_EN), .Q(register_5_q), .clk(CLK), .clr(or_1_out));
  Register register_6 (.D(register_12_q), .en(WRITE_EN), .Q(register_6_q), .clk(CLK), .clr(or_1_out));
  Adder #(.width(32)) adder_1 (
    .a({register_7_q, register_5_q, register_3_q, register_1_q}), .b({register_12_q, register_8_q}),
    .out(adder_1_out));  // open: cin, cout
  Subtractor #(.width(32)) subtractor_2 (
    .a({register_7_q, register_5_q, register_3_q, register_1_q}), .b({register_12_q, register_8_q}),
    .out(subtractor_2_out));  // open: bin, bout
  Multiplier #(.width(32)) multiplier_1 (
    .a({register_7_q, register_5_q, register_3_q, register_1_q}), .b({register_12_q, register_8_q}),
    .out(multiplier_1_out));  // open: cin, cout
  Divider #(.width(32)) divider_1 (
    .a({register_7_q, register_5_q, register_3_q, register_1_q}), .b({register_12_q, register_8_q}),
    .out(divider_1_out));  // open: upper, rem
  Register register_7 (.D(register_5_q), .en(WRITE_EN), .Q(register_7_q), .clk(CLK), .clr(or_1_out));
  BitSelector #(.group(3)) bitselector_2 (.in(register_6_q), .out(bitselector_2_out), .sel(2'b00));
  Multiplexer #(.select(3), .width(32), .enable("false")) multiplexer_1 (
    .in0({32{1'b0}}), .in1(adder_1_out), .in2(subtractor_2_out), .in3(multiplier_1_out), .in4(divider_1_out),
    .in5({32{1'b0}}), .in6({32{1'b0}}), .in7({32{1'b0}}), .out(multiplexer_1_out), .sel(bitselector_2_out));
  Register register_8 (.D(register_7_q), .en(WRITE_EN), .Q(register_8_q[7:0]), .clk(CLK), .clr(or_1_out));
  or or_2 (or_2_out, bitselector_2_out[0], bitselector_2_out[1], bitselector_2_out[2]);
  Register register_9 (.D(register_8_q[7:0]), .en(WRITE_EN), .Q(register_8_q[15:8]), .clk(CLK), .clr(or_1_out));
  Register #(.width(32)) register_10 (
    .D(multiplexer_1_out), .en(or_2_out), .Q(register_10_q), .clk(CLK), .clr(or_1_out));
  Register register_11 (.D(register_8_q[15:8]), .en(WRITE_EN), .Q(register_8_q[23:16]), .clk(CLK), .clr(or_1_out));
  Register register_12 (.D(register_8_q[23:16]), .en(WRITE_EN), .Q(register_12_q), .clk(CLK), .clr(or_1_out));
endmodule
